# Fritzing sketch electronics (saved by Fritzing 0.8.5b)
circuit board: 5.97959cm x 5.6268cm
breadboards: 1

parts:
  C1 = Ceramic Capacitor [capacitance=100nF package="100 mil [THT, multilayer]"]
  R3 = Photocell (LDR) [package=THT]
  Arduino_nano = Arduino Nano (Rev3.0)
  Power_plug = Power plug
  R2 = Resistor [tolerance=±5% resistance=10k package=THT]
  R1 = Resistor [tolerance=±5% resistance=2.4k package=THT]
  J1 = female pin header, 4 pins [form="♀ (female)"]
  J2 = female pin header, 4 pins [form="♀ (female)"]

nets (from the pcb view):
  N1: C1.0, Arduino_nano.D2, R1.Pin_1
  GND: C1.1, Arduino_nano.GND, Power_plug.GND, R2.Pin_1, J1.pin4
  N2: R3.pin_0, Arduino_nano.5V
  N3: R3.pin_1, R2.Pin_0, R1.Pin_0
  N4: Arduino_nano.D8, J1.pin2
  N5: Arduino_nano.D11/MOSI, J1.pin3
  N6: Arduino_nano.D12/MISO, J2.pin4
  VIN: Arduino_nano.VIN, Power_plug.VCC
  N7: Arduino_nano.3V3, J1.pin1
  N8: Arduino_nano.D13/SCK, J2.pin3
